# Fritzing sketch balancing_circuit (saved by Fritzing 0.9.3b)

parts:
  S1 = H-Bridge with L298N
  M1 = DC Motor
  M2 = DC Motor
  GY1 = MPU-6050 Board GY-521 [form="♀ (female)" package=THT]
  BAT1 = BC9VPC [package=bc9vpc]
  부품1 = Arduino Uno (Rev3)

nets:
  N1: S1.12V, BAT1.V+
  GND: S1.GND, GY1.pin2, BAT1.V-, 부품1.GND
  5V: S1.5V, 부품1.VIN
  N2: S1.ENA, 부품1.D9_PWM
  N3: S1.IN1, 부품1.D7
  N4: S1.IN2, 부품1.D6_PWM
  N5: S1.IN3, 부품1.D5_PWM
  N6: S1.IN4, 부품1.D4
  N7: S1.ENB, 부품1.D3_PWM
  N8: S1.M1-01, M1.pin_2
  N9: S1.M1-02, M1.pin_1
  N10: S1.M2-01, M2.pin_2
  N11: S1.M2-02, M2.pin_1
  N12: GY1.pin1, 부품1.5V
  N13: GY1.pin3, 부품1.A5/SCL
  N14: GY1.pin4, 부품1.A4/SDA
  N15: GY1.pin8, 부품1.D2

custom parts:
  H-Bridge with L298N: h-bridge
  MPU-6050 Board GY-521: Acelerometro y Giroscopio MPU-6050 Board GY-521
